// Logisim project exer1&2.circ as structural Verilog: 6 circuits, main circuit main
module main (
  input  [7:0] in_1,
  output [7:0] out_2,
  output [7:0] out_3
);

  AddMachine addmachine_1 (.in_1(in_1), .out_2(out_2), .out_3(out_3));
endmodule

module NAND (
  input  in_1,
  input  in_2,
  output out_3
);

  wire and_1_out;

  and and_1 (and_1_out, in_1, in_2, in_2);
  not not_1 (out_3, and_1_out);
endmodule

module XOR (
  input  in_1,
  input  in_2,
  output out_3
);

  wire and_1_out, and_2_out, not_1_out, not_2_out;

  not not_1 (not_1_out, in_1);
  not not_2 (not_2_out, in_2);
  and and_1 (and_1_out, not_1_out, in_2);
  and and_2 (and_2_out, in_1, not_2_out);
  or or_1 (out_3, and_1_out, and_2_out);
endmodule

module _2_to_1_MUX (
  input  in_1,
  input  in_2,
  input  in_3,
  output out_4
);

  wire and_1_out, and_2_out, not_1_out;

  not not_1 (not_1_out, in_2);
  and and_1 (and_1_out, not_1_out, in_1);
  and and_2 (and_2_out, in_2, in_3);
  or or_1 (out_4, and_1_out, and_2_out);
endmodule

module _4_to_1_MUX (
  input  in_1,
  input  in_2,
  input  in_3,
  input  in_4,
  input  in_5,
  input  in_6,
  output out_7
);

  wire n2_to_1_mux_1_out_4, n2_to_1_mux_2_out_4;

  _2_to_1_MUX u_2_to_1_mux_1 (.in_1(in_1), .in_2(in_3), .in_3(in_2), .out_4(n2_to_1_mux_1_out_4));
  _2_to_1_MUX u_2_to_1_mux_2 (.in_1(in_3), .in_2(in_4), .in_3(in_5), .out_4(n2_to_1_mux_2_out_4));
  _2_to_1_MUX u_2_to_1_mux_3 (.in_1(n2_to_1_mux_1_out_4), .in_2(in_6), .in_3(n2_to_1_mux_2_out_4), .out_4(out_7));
endmodule

module AddMachine (
  input  [7:0] in_1,
  output [7:0] out_2,
  output [7:0] out_3
);

  wire clock_1_out;

  Adder adder_1 (.a(in_1), .b(out_3), .out(out_2));  // open: cin, cout
  Register register_1 (.D(out_2), .Q(out_3), .clk(clock_1_out));  // open: en, clr
  Clock clock_1 (.out(clock_1_out));
endmodule
