// Logisim project exerA.circ as structural Verilog
module Ex1 (
  input  [7:0] In1,
  output Out1,
  output [7:0] Out2
);

  not not_1 (Out2[7], In1[7]);
  and and_1 (Out1, In1[0], In1[7]);

  assign Out2[6:0] = In1[6:0];
endmodule

module rotr (
  input  [15:0] A,
  input  [3:0] B,
  output [15:0] out_3
);

  wire undriven;
  wire [15:0] multiplexer_1_out, multiplexer_2_out, multiplexer_3_out, rotate1_1_out_2, rotate1_2_out_2,
       rotate1_3_out_2, rotate1_4_out_2, rotate1_5_out_2, rotate1_6_out_2, rotate1_7_out_2, rotate1_8_out_2,
       rotate1_9_out_2, rotate1_10_out_2, rotate1_11_out_2, rotate1_13_out_2, rotate1_14_out_2,
       rotate1_15_out_2;

  Multiplexer #(.width(16)) multiplexer_1 (
    .in0(A), .in1(rotate1_1_out_2), .out(multiplexer_1_out), .sel(B[0]));  // open: en
  rotate1 rotate1_1 (.in_1(A), .out_2(rotate1_1_out_2));
  rotate1 rotate1_2 (.in_1(multiplexer_1_out), .out_2(rotate1_2_out_2));
  Multiplexer #(.width(16)) multiplexer_2 (
    .in0(multiplexer_1_out), .in1(rotate1_3_out_2), .out(multiplexer_2_out), .sel(B[1]), .en(undriven));
  rotate1 rotate1_3 (.in_1(rotate1_2_out_2), .out_2(rotate1_3_out_2));
  rotate1 rotate1_4 (.in_1(multiplexer_2_out), .out_2(rotate1_4_out_2));
  rotate1 rotate1_5 (.in_1(rotate1_4_out_2), .out_2(rotate1_5_out_2));
  rotate1 rotate1_6 (.in_1(rotate1_7_out_2), .out_2(rotate1_6_out_2));
  rotate1 rotate1_7 (.in_1(multiplexer_3_out), .out_2(rotate1_7_out_2));
  rotate1 rotate1_8 (.in_1(rotate1_9_out_2), .out_2(rotate1_8_out_2));
  rotate1 rotate1_9 (.in_1(rotate1_13_out_2), .out_2(rotate1_9_out_2));
  rotate1 rotate1_10 (.in_1(rotate1_5_out_2), .out_2(rotate1_10_out_2));
  rotate1 rotate1_11 (.in_1(rotate1_10_out_2), .out_2(rotate1_11_out_2));
  rotate1 rotate1_12 (.in_1(rotate1_6_out_2));  // open: out_2
  rotate1 rotate1_13 (.out_2(rotate1_13_out_2));  // open: in_1
  rotate1 rotate1_14 (.in_1(rotate1_8_out_2), .out_2(rotate1_14_out_2));
  rotate1 rotate1_15 (.in_1(rotate1_14_out_2), .out_2(rotate1_15_out_2));
  Multiplexer #(.width(16)) multiplexer_3 (
    .in0(multiplexer_2_out), .in1(rotate1_11_out_2), .out(multiplexer_3_out), .sel(B[2]));  // open: en
  Multiplexer #(.width(16)) multiplexer_4 (
    .in0(multiplexer_3_out), .in1(rotate1_15_out_2), .out(out_3), .sel(B[3]));  // open: en
endmodule

module rotate1 (
  input  [15:0] in_1,
  output [15:0] out_2
);


  assign out_2 = {in_1[0], in_1[15:1]};
endmodule
