// Logisim project cpu.circ as structural Verilog: 5 circuits, main circuit main
module main (
  input  [31:0] RS_READ_VALUE,
  input  [31:0] RT_READ_VALUE,
  input  [31:0] INSTRUCTION,
  input  CLOCK,
  input  RESET,
  output [31:0] t0,
  output [31:0] t1,
  output [31:0] t2,
  output [31:0] t3,
  output [4:0] RS,
  output [4:0] RT,
  output [4:0] Write_Register,
  output [31:0] RD_WRITE_VALUE,
  output RD_WRITE_ENABLE,
  output [23:0] FETCH_ADDRESS
);

  wire Access_Byte, ALU_signed_overflow, ALUSrc, and_2_out, and_3_out, and_4_out, beq, bne,
       control_1_writereg, DoBranch, equal, j, jal, jr, Jump, kill, kill_instr, MemtoReg, RegDst, regfile_rd,
       regfile_rs, regfile_rt, RegWr, shift, WriteMem;
  wire [1:0] read_reg1, read_reg2, write_reg;
  wire [4:0] multiplexer_7_out, multiplexer_15_out, multiplexer_17_out, reg_rd, reg_rt;
  wire [5:0] multiplexer_11_out, newFunct;
  wire [15:0] addr;
  wire [23:0] adder_1_out, adder_2_out, bit_extender_2_out, bit_extender_4_out, bit_extender_6_out,
       multiplexer_1_out, multiplexer_9_out, multiplexer_13_out, PC_1;
  wire [25:0] subtractor_1_out;
  wire [31:0] bit_extender_1_out, bit_extender_7_out, busB, DataOut, multiplexer_2_out, multiplexer_5_out,
       multiplexer_10_out, multiplexer_16_out, newX, newY, Ra, Rb, result, subtractor_2_out, x, y;
  wire [31:26] Instruction_t;

  and and_1 (RD_WRITE_ENABLE, RegWr, ~jr);  // AND_Gate
  Adder #(.width(24)) adder_1 (.a(24'h1), .b(FETCH_ADDRESS), .out(adder_1_out));  // open: cin, cout
  Multiplexer #(.width(24)) multiplexer_1 (
    .in0(adder_1_out), .in1(FETCH_ADDRESS), .out(multiplexer_1_out), .sel(kill));  // open: en
  Register #(.width(24)) register_1 (.D(multiplexer_1_out), .Q(PC_1), .clk(CLOCK));  // open: en, clr
  Multiplexer #(.width(32)) multiplexer_2 (
    .in0(INSTRUCTION), .in1({32{1'b0}}), .out(multiplexer_2_out), .sel(kill));  // open: en
  I_Type_handling i_type_handling_1 (
    .rs_read(x), .Immediate(addr), .Opcode(Instruction_t), .newX(newX), .newY(newY), .newFunct(newFunct));
  Register #(.width(32)) register_2 (
    .D(multiplexer_2_out), .Q({Instruction_t, RS, RT, addr}), .clk(CLOCK));  // open: en, clr
  and and_2 (and_2_out, RegWr, ~jr);  // AND_Gate
  shift_checker shift_checker_1 (.funct(addr[5:0]), .RegDst(RegDst), .Shift(shift));
  regfile_main RegFile (
    .Read_register_1(read_reg1), .Read_register_2(read_reg2), .write_register(write_reg),
    .write_data(RD_WRITE_VALUE), .t0_Value(t0), .t1_Value(t1), .t2_Value(t2), .t3_Value(t3),
    .RegWrite(and_2_out), .clock(CLOCK), .Read_Data_1(Ra), .Read_Data_2(Rb));
  register_check register_check_1 (.in_1(RS), .out_2(regfile_rs));
  register_check register_check_2 (.in_1(RT), .out_2(regfile_rt));
  register_check register_check_3 (.in_1(addr[15:11]), .out_2(regfile_rd));
  assign bit_extender_1_out = {{27{1'b0}}, addr[10:6]};  // Bit_Extender bit_extender_1
  Multiplexer #(.width(32)) multiplexer_3 (.in0(RS_READ_VALUE), .in1(Ra), .out(x), .sel(regfile_rs));  // open: en
  Multiplexer #(.width(32)) multiplexer_4 (.in0(RT_READ_VALUE), .in1(Rb), .out(busB), .sel(regfile_rt));  // open: en
  Multiplexer #(.width(32)) multiplexer_5 (
    .in0(busB), .in1(bit_extender_1_out), .out(multiplexer_5_out), .sel(shift));  // open: en
  assign bit_extender_2_out = {{8{addr[15]}}, addr};  // Bit_Extender bit_extender_2
  Subtractor #(.width(26)) subtractor_1 (
    .a({RS, RT, addr}), .b(26'h100000), .out(subtractor_1_out));  // open: bin, bout
  Multiplexer #(.width(32)) multiplexer_6 (.in0(multiplexer_5_out), .in1(newY), .out(y), .sel(ALUSrc));  // open: en
  Bit_Extender #(.in_width(5), .out_width(2)) bit_extender_3 (.in(multiplexer_7_out), .out(read_reg1));
  Multiplexer #(.width(5)) multiplexer_7 (.in1(RS), .out(multiplexer_7_out), .sel(regfile_rs));  // open: in0, en
  Multiplexer #(.width(5)) multiplexer_8 (.in1(RT), .out(reg_rt), .sel(regfile_rt));  // open: in0, en
  Multiplexer #(.width(24)) multiplexer_9 (
    .in0(PC_1), .in1(adder_2_out), .out(multiplexer_9_out), .sel(DoBranch));  // open: en
  Adder #(.width(24)) adder_2 (.a(PC_1), .b(bit_extender_2_out), .out(adder_2_out));  // open: cin, cout
  Bit_Extender #(.in_width(26), .out_width(24), .\type ("sign")) bit_extender_4 (
    .in(subtractor_1_out), .out(bit_extender_4_out));
  Multiplexer #(.width(32)) multiplexer_10 (.in0(x), .in1(newX), .out(multiplexer_10_out), .sel(ALUSrc));  // open: en
  alu_main ALU (
    .Switch__S(multiplexer_11_out), .X(multiplexer_10_out), .Equal(equal), .RESULT(result),
    .Signed_Overflow(ALU_signed_overflow), .Y(y));
  Multiplexer #(.width(6)) multiplexer_11 (
    .in0(addr[5:0]), .in1(newFunct), .out(multiplexer_11_out), .sel(ALUSrc));  // open: en
  Multiplexer #(.width(5)) multiplexer_12 (.in1(addr[15:11]), .out(reg_rd), .sel(regfile_rd));  // open: in0, en
  Bit_Extender #(.in_width(5), .out_width(2)) bit_extender_5 (.in(reg_rt), .out(read_reg2));
  Multiplexer #(.width(24)) multiplexer_13 (
    .in0(multiplexer_9_out), .in1(bit_extender_4_out), .out(multiplexer_13_out), .sel(Jump));  // open: en
  Bit_Extender #(.in_width(32), .out_width(24), .\type ("sign")) bit_extender_6 (
    .in(subtractor_2_out), .out(bit_extender_6_out));
  Subtractor #(.width(32)) subtractor_2 (.a(x), .b(32'h100000), .out(subtractor_2_out));  // open: bin, bout
  LED Signed_Overflow (.in(ALU_signed_overflow));
  Multiplexer #(.width(24)) multiplexer_14 (
    .in0(multiplexer_13_out), .in1(bit_extender_6_out), .out(FETCH_ADDRESS), .sel(jr));  // open: en
  control control_1 (
    .opcode(Instruction_t), .RegDst(RegDst), .ALUSrc(ALUSrc), .MemtoReg(MemtoReg), .Access_Byte(Access_Byte),
    .WriteReg(control_1_writereg), .WriteMem(WriteMem), .beq(beq), .j(j), .bne(bne), .jal(jal));
  Multiplexer #(.width(5)) multiplexer_15 (
    .in0(RT), .in1(addr[15:11]), .out(multiplexer_15_out), .sel(RegDst));  // open: en
  mem_main MEM (
    .Data_Mem_Addr(result), .Data_Mem_In(busB), .ACCESS_BYTE(Access_Byte), .MEM_WRITE(WriteMem),
    .CLOCK(CLOCK), .Data_Mem_Out(DataOut));
  Multiplexer #(.width(32)) multiplexer_16 (
    .in0(result), .in1(DataOut), .out(multiplexer_16_out), .sel(MemtoReg));  // open: en
  assign bit_extender_7_out = {{8{PC_1[23]}}, PC_1};  // Bit_Extender bit_extender_7
  Multiplexer #(.width(5)) multiplexer_17 (
    .in0(reg_rt), .in1(reg_rd), .out(multiplexer_17_out), .sel(RegDst));  // open: en
  Multiplexer #(.width(5)) multiplexer_18 (
    .in0(multiplexer_15_out), .in1({5{1'b1}}), .out(Write_Register), .sel(jal));  // open: en
  Comparator #(.width(6)) comparator_1 (.a(addr[5:0]), .b(6'b001000), .eq(jr));  // open: gt, lt
  and and_3 (and_3_out, equal, beq);
  and and_4 (and_4_out, ~equal, bne);  // AND_Gate
  Multiplexer #(.width(32)) multiplexer_19 (
    .in0(multiplexer_16_out), .in1(bit_extender_7_out), .out(RD_WRITE_VALUE), .sel(jal));  // open: en
  Bit_Extender #(.in_width(5), .out_width(2)) bit_extender_8 (.in(multiplexer_17_out), .out(write_reg));
  or or_1 (DoBranch, and_3_out, and_4_out);
  Comparator #(.width(32)) comparator_2 (
    .a({Instruction_t, RS, RT, addr}), .b({32{1'b0}}), .eq(kill_instr));  // open: gt, lt
  and and_5 (RegWr, ~kill_instr, control_1_writereg);  // AND_Gate
  or or_2 (Jump, j, jal);
  or or_3 (kill, Jump, jr, DoBranch);

  // Other names for the same wires on the sheet: clk = CLOCK; DataToWr[31:0] = RD_WRITE_VALUE;
  //   Fetch[23:0] = FETCH_ADDRESS; funct[5:0] = addr[5:0]; immed[15:0] = addr; Instruction_t[25:0] = {RS, RT, addr};
  //   shamt[4:0] = addr[10:6]; RD[4:0] = addr[15:11]; addr[25:16] = {RS, RT}; opcode[5:0] = Instruction_t;
  //   rs_read[31:0] = RS_READ_VALUE; rt_read[31:0] = RT_READ_VALUE

  // Notes on the sheet:
  //   PC + 1
  //   These are outputs/inputs from run.circ
  //   I-type handling
  //   These are outputs to run.circ
  //   What is our next address?
  //   If our instruction is "jr"
  //   Determine if we branch
endmodule

module register_check (
  input  [4:0] in_1,
  output out_2
);

  wire comparator_1_lt, comparator_2_gt;

  Comparator #(.width(5), .mode("unsigned")) comparator_1 (
    .a(in_1), .b(5'b01100), .lt(comparator_1_lt));  // open: gt, eq
  Comparator #(.width(5), .mode("unsigned")) comparator_2 (
    .a(in_1), .b(5'b00111), .gt(comparator_2_gt));  // open: eq, lt
  and and_1 (out_2, comparator_1_lt, comparator_2_gt);
endmodule

module control (
  input  [5:0] opcode,
  output RegDst,
  output ALUSrc,
  output MemtoReg,
  output Access_Byte,
  output WriteReg,
  output WriteMem,
  output beq,
  output j,
  output bne,
  output jal
);

  wire immed_out, lb_out, lbu_out, lw_out;

  and R_Type (RegDst, ~opcode[5], ~opcode[4], ~opcode[3], ~opcode[2], ~opcode[1], ~opcode[0]);  // AND_Gate
  and immed (immed_out, ~opcode[5], ~opcode[4], opcode[3]);  // AND_Gate
  and sw (WriteMem, opcode[5], ~opcode[4], opcode[3], ~opcode[2], opcode[1], opcode[0]);  // AND_Gate
  and lb (lb_out, opcode[5], ~opcode[4], ~opcode[3], ~opcode[2], ~opcode[1], ~opcode[0]);  // AND_Gate
  and lbu (lbu_out, opcode[5], ~opcode[4], ~opcode[3], opcode[2], ~opcode[1], ~opcode[0]);  // AND_Gate
  and lw (lw_out, opcode[5], ~opcode[4], ~opcode[3], ~opcode[2], opcode[1], opcode[0]);  // AND_Gate
  and u_beq (beq, ~opcode[5], ~opcode[4], ~opcode[3], opcode[2], ~opcode[1], ~opcode[0]);  // AND_Gate
  and u_j (j, ~opcode[5], ~opcode[4], ~opcode[3], ~opcode[2], opcode[1], ~opcode[0]);  // AND_Gate
  and u_bne (bne, ~opcode[5], ~opcode[4], ~opcode[3], opcode[2], ~opcode[1], opcode[0]);  // AND_Gate
  and u_jal (jal, ~opcode[5], ~opcode[4], ~opcode[3], ~opcode[2], opcode[1], opcode[0]);  // AND_Gate
  or or_1 (ALUSrc, immed_out, WriteMem, lb_out, lbu_out, lw_out);
  or or_2 (MemtoReg, lb_out, lbu_out, lw_out);
  or or_3 (Access_Byte, lb_out, lbu_out);
  nor nor_1 (WriteReg, WriteMem, beq, j, bne);

  // Notes on the sheet:
  //   Also works as ReadMem
  //   If not sw, beq, bne, j 
endmodule

module I_Type_handling (
  input  [31:0] rs_read,
  input  [15:0] Immediate,
  input  [5:0] Opcode,
  output [31:0] newX,
  output [31:0] newY,
  output [5:0] newFunct
);

  wire andi, lui, or_1_out, or_2_out, ori;
  wire [5:0] multiplexer_2_out, multiplexer_3_out;
  wire [31:0] bit_extender_1_out, bit_extender_2_out, immed;

  Comparator #(.width(6)) comparator_1 (.a(Opcode), .b(6'b001100), .eq(andi));  // open: gt, lt
  Comparator #(.width(6)) comparator_2 (.a(Opcode), .b(6'b001101), .eq(ori));  // open: gt, lt
  Comparator #(.width(6)) comparator_3 (.a(Opcode), .b(6'b001111), .eq(lui));  // open: gt, lt
  assign bit_extender_1_out = {{16{Immediate[15]}}, Immediate};  // Bit_Extender bit_extender_1
  Multiplexer #(.width(32)) multiplexer_1 (
    .in0(bit_extender_1_out), .in1(bit_extender_2_out), .out(immed), .sel(or_1_out));  // open: en
  assign bit_extender_2_out = {{16{1'b0}}, Immediate};  // Bit_Extender bit_extender_2
  or or_1 (or_1_out, andi, ori, lui);
  Multiplexer #(.width(6)) multiplexer_2 (
    .in0({6{1'b0}}), .in1(6'b100101), .out(multiplexer_2_out), .sel(ori));  // open: en
  Multiplexer #(.width(6)) multiplexer_3 (
    .in0(multiplexer_2_out), .in1(6'b100100), .out(multiplexer_3_out), .sel(andi));  // open: en
  or or_2 (or_2_out, andi, ori, lui);
  Multiplexer #(.width(32)) multiplexer_4 (.in0(rs_read), .in1(immed), .out(newX), .sel(lui));  // open: en
  Multiplexer #(.width(32)) multiplexer_5 (.in0(immed), .in1(32'h10), .out(newY), .sel(lui));  // open: en
  Multiplexer #(.width(6)) multiplexer_6 (
    .in0(6'b100001), .in1(multiplexer_3_out), .out(newFunct), .sel(or_2_out));  // open: en

  // Other names for the same wires on the sheet: oldX[31:0] = rs_read

  // Notes on the sheet:
  //   All will be addu functions EXCEPT andi, ori, and lui
endmodule

module shift_checker (
  input  [5:0] funct,
  input  RegDst,
  output Shift
);

  wire or_1_out, sll___srl_out, sra_out;

  and sll___srl (sll___srl_out, ~funct[5], ~funct[4], ~funct[3], ~funct[2], ~funct[0]);  // AND_Gate
  and sra (sra_out, ~funct[5], ~funct[4], ~funct[3], ~funct[2], funct[1], funct[0]);  // AND_Gate
  or or_1 (or_1_out, sll___srl_out, sra_out);
  and and_1 (Shift, or_1_out, RegDst);

  // Notes on the sheet:
  //   Check if R-Type
endmodule
