// Logisim project mem.circ as structural Verilog: 1 circuit, main circuit main
module main (
  input  [31:0] Data_Mem_Addr,
  input  [31:0] Data_Mem_In,
  input  ACCESS_BYTE,
  input  MEM_WRITE,
  input  CLOCK,
  output [31:0] Data_Mem_Out
);

  wire not_1_out;
  wire [7:0] bit_extender_3_out;
  wire [23:0] bit_extender_1_out;
  wire [31:0] bit_extender_2_out, ram_1_data, subtractor_1_out;

  Subtractor #(.width(32)) subtractor_1 (
    .a(Data_Mem_Addr), .b(32'h10010000), .out(subtractor_1_out));  // open: bin, bout
  Bit_Extender #(.in_width(32), .out_width(24)) bit_extender_1 (.in(subtractor_1_out), .out(bit_extender_1_out));
  RAM #(.addrWidth(24), .dataWidth(32)) ram_1 (
    .addr(bit_extender_1_out), .data(ram_1_data), .sel(1'b1), .clk(CLOCK), .ld(not_1_out), .clr(1'b0));
  not not_1 (not_1_out, MEM_WRITE);
  assign ram_1_data = MEM_WRITE ? Data_Mem_In : 32'bz;  // Controlled_Buffer controlled_buffer_1
  assign bit_extender_2_out = {{24{1'b0}}, bit_extender_3_out};  // Bit_Extender bit_extender_2
  Bit_Extender #(.in_width(32), .out_width(8)) bit_extender_3 (.in(ram_1_data), .out(bit_extender_3_out));
  Multiplexer #(.width(32)) multiplexer_1 (
    .in0(ram_1_data), .in1(bit_extender_2_out), .out(Data_Mem_Out), .sel(ACCESS_BYTE));  // open: en

  // Other names for the same wires on the sheet: clk = CLOCK

  // Notes on the sheet:
  //   These are INPUTS to the circuit
  //   These are INPUTS to the circuit
  //   DO NOT CHANGE THE LOCATIONS OF THE INPUTS/OUTPUTS! IF YOU DO SO, YOU NEED TO MAKE SURE THE PINS ARE AT THE RIGHT PLACE!
  //   Yet again, the clock is not an actual clock, but an input, one that will be driven from a higher circuit
  //   This is an OUTPUT to the circuit
endmodule
