// Logisim project alu.circ as structural Verilog: 5 circuits, main circuit main
module main (
  input  [31:0] X,
  input  [31:0] Y,
  input  [5:0] Switch__S,
  output Signed_Overflow,
  output [31:0] RESULT,
  output Equal
);

  wire add_overflow, and_2_out, and_3_out, comparator_2_lt, comparator_3_lt, comparator_4_eq,
       comparator_5_eq, sub_overflow;
  wire [4:0] bit_extender_1_out, bit_extender_2_out, bit_extender_3_out;
  wire [4:4] _5_Bit_Switch;
  wire [31:0] add, addu, \and , bitpal, lfsr, \or , sll, slt, sltu, sra, srl, sub, subu;

  xor xor_1 (_5_Bit_Switch[4], Switch__S[5], Switch__S[4]);
  Bit_Extender #(.in_width(32), .out_width(5)) bit_extender_1 (.in(Y), .out(bit_extender_1_out));
  Bit_Extender #(.in_width(32), .out_width(5)) bit_extender_2 (.in(Y), .out(bit_extender_2_out));
  Bit_Extender #(.in_width(32), .out_width(5)) bit_extender_3 (.in(Y), .out(bit_extender_3_out));
  Shifter #(.width(32)) shifter_1 (.in(X), .\dist (bit_extender_1_out), .out(sll));
  Shifter #(.width(32), .shift("lr")) shifter_2 (.in(X), .\dist (bit_extender_2_out), .out(srl));
  Shifter #(.width(32), .shift("ar")) shifter_3 (.in(X), .\dist (bit_extender_3_out), .out(sra));
  bitpal bitpal_1 (.in_1(X), .out(bitpal));
  assign \or  = X | Y;  // OR_Gate or_1, 32 bits wide
  add add_1 (.in_1(X), .in_2(Y), .out(add), .overflow(add_overflow));
  Adder #(.width(32)) adder_1 (.a(X), .b(Y), .out(addu));  // open: cin, cout
  Comparator #(.width(32)) comparator_1 (.a(X), .b(Y), .eq(Equal));  // open: gt, lt
  Comparator #(.width(32)) comparator_2 (.a(X), .b(Y), .lt(comparator_2_lt));  // open: gt, eq
  assign slt = {{31{1'b0}}, comparator_2_lt};  // Bit_Extender bit_extender_4
  Comparator #(.width(32), .mode("unsigned")) comparator_3 (.a(X), .b(Y), .lt(comparator_3_lt));  // open: gt, eq
  assign sltu = {{31{1'b0}}, comparator_3_lt};  // Bit_Extender bit_extender_5
  lfsr lfsr_1 (.in_1(X), .out(lfsr));
  assign \and  = X & Y;  // AND_Gate and_1, 32 bits wide
  sub sub_1 (.in_1(X), .in_2(Y), .out(sub), .overflow(sub_overflow));
  Subtractor #(.width(32)) subtractor_1 (.a(X), .b(Y), .out(subu));  // open: bin, bout
  Comparator #(.width(5)) comparator_4 (
    .a({_5_Bit_Switch[4], Switch__S[3:0]}), .b(5'b10010), .eq(comparator_4_eq));  // open: gt, lt
  Comparator #(.width(5)) comparator_5 (
    .a({_5_Bit_Switch[4], Switch__S[3:0]}), .b(5'b10000), .eq(comparator_5_eq));  // open: gt, lt
  Multiplexer #(.select(5), .width(32)) multiplexer_1 (
    .in0(sll), .in2(srl), .in3(sra), .in14(bitpal), .in15(lfsr), .in16(add), .in17(addu), .in18(sub),
    .in19(subu), .in20(\and ), .in21(\or ), .in26(slt), .in27(sltu), .out(RESULT),
    .sel({_5_Bit_Switch[4], Switch__S[3:0]}));  // open: in1, in4, in5, in6, in7, in8, in9, in10, in11, in12, in13, in22, in23, in24, in25, in28, in29, in30, in31, en
  and and_2 (and_2_out, comparator_4_eq, sub_overflow);
  and and_3 (and_3_out, comparator_5_eq, add_overflow);
  or or_2 (Signed_Overflow, and_2_out, and_3_out);

  // Other names for the same wires on the sheet: _5_Bit_Switch[3:0] = Switch__S[3:0]

  // Notes on the sheet:
  //   INPUTS to your circuit
  //   INPUT to your circuit
  //   This will turn 11,00->0 and 10,01->1
  //   letting us use a 5 bit selector
  //   This works since instructions
  //   starting with 11 and 00
  //   them
  //   DON'T CHANGE THE INPUTS AND OUTPUTS! IF YOU DO SO, YOU NEED TO MAKE SURE THE PINS ARE IN THE RIGHT PLACES!
  //   OUTPUTS of your circuit
endmodule

module bitpal (
  input  [31:0] in_1,
  output [31:0] out
);

  wire comparator_1_eq;

  Comparator #(.width(16)) comparator_1 (
    .a({in_1[0], in_1[1], in_1[2], in_1[3], in_1[4], in_1[5], in_1[6], in_1[7], in_1[8], in_1[9], in_1[10], in_1[11], in_1[12], in_1[13], in_1[14], in_1[15]}),
    .b(in_1[31:16]), .eq(comparator_1_eq));  // open: gt, lt
  assign out = {{31{1'b0}}, comparator_1_eq};  // Bit_Extender bit_extender_1
endmodule

module lfsr (
  input  [31:0] in_1,
  output [31:0] out
);

  ExactlyOne xor_1 (.out(out[31]), .in0(in_1[0]), .in1(in_1[2]), .in2(in_1[3]), .in3(in_1[5]));

  assign out[30:0] = in_1[31:1];
endmodule

module add (
  input  [31:0] in_1,
  input  [31:0] in_2,
  output [31:0] out,
  output overflow
);

  wire [30:0] and_1_out;
  wire [31:0] xor_1_out, xor_2_out;

  Adder #(.width(32)) adder_1 (.a(in_1), .b(in_2), .out(out));  // open: cin, cout
  assign xor_1_out = in_1 ^ out;  // XOR_Gate xor_1, 32 bits wide
  assign xor_2_out = out ^ in_2;  // XOR_Gate xor_2, 32 bits wide
  assign {overflow, and_1_out} = xor_1_out & xor_2_out;  // AND_Gate and_1, 32 bits wide
endmodule

module sub (
  input  [31:0] in_1,
  input  [31:0] in_2,
  output [31:0] out,
  output overflow
);

  wire [30:0] and_1_out;

  Subtractor #(.width(32)) subtractor_1 (.a(in_1), .b(in_2), .out(out));  // open: bin, bout
  assign {overflow, and_1_out} = out & in_2;  // AND_Gate and_1, 32 bits wide
endmodule
