// Logisim project regfile.circ as structural Verilog: 1 circuit, main circuit main
module main (
  input  [1:0] Read_register_1,
  input  [1:0] Read_register_2,
  input  [1:0] write_register,
  input  [31:0] write_data,
  input  RegWrite,
  input  clock,
  output [31:0] t0_Value,
  output [31:0] t1_Value,
  output [31:0] t2_Value,
  output [31:0] t3_Value,
  output [31:0] Read_Data_1,
  output [31:0] Read_Data_2
);

  wire [31:0] multiplexer_2_out, multiplexer_5_out, multiplexer_7_out, multiplexer_8_out, t0_write, t1_write,
       t2_write, t3_write;

  Register #(.width(32)) t0 (.D(t0_write), .Q(t0_Value), .clk(clock));  // open: en, clr
  Register #(.width(32)) t1 (.D(t1_write), .Q(t1_Value), .clk(clock));  // open: en, clr
  Multiplexer #(.width(32)) multiplexer_1 (
    .in0(t3_Value), .in1(multiplexer_2_out), .out(t3_write), .sel(RegWrite));  // open: en
  Multiplexer #(.select(2), .width(32)) multiplexer_2 (
    .in0(t3_Value), .in1(t3_Value), .in2(t3_Value), .in3(write_data), .out(multiplexer_2_out),
    .sel(write_register));  // open: en
  Register #(.width(32)) t2 (.D(t2_write), .Q(t2_Value), .clk(clock));  // open: en, clr
  Multiplexer #(.select(2), .width(32)) multiplexer_3 (
    .in0(t0_Value), .in1(t1_Value), .in2(t2_Value), .in3(t3_Value), .out(Read_Data_1), .sel(Read_register_1));  // open: en
  Register #(.width(32)) t3 (.D(t3_write), .Q(t3_Value), .clk(clock));  // open: en, clr
  Multiplexer #(.width(32)) multiplexer_4 (
    .in0(t2_Value), .in1(multiplexer_5_out), .out(t2_write), .sel(RegWrite));  // open: en
  Multiplexer #(.select(2), .width(32)) multiplexer_5 (
    .in0(t2_Value), .in1(t2_Value), .in2(write_data), .in3(t2_Value), .out(multiplexer_5_out),
    .sel(write_register));  // open: en
  Multiplexer #(.select(2), .width(32)) multiplexer_6 (
    .in0(t0_Value), .in1(t1_Value), .in2(t2_Value), .in3(t3_Value), .out(Read_Data_2), .sel(Read_register_2));  // open: en
  Multiplexer #(.select(2), .width(32)) multiplexer_7 (
    .in0(write_data), .in1(t0_Value), .in2(t0_Value), .in3(t0_Value), .out(multiplexer_7_out),
    .sel(write_register));  // open: en
  Multiplexer #(.select(2), .width(32)) multiplexer_8 (
    .in0(t1_Value), .in1(write_data), .in2(t1_Value), .in3(t1_Value), .out(multiplexer_8_out),
    .sel(write_register));  // open: en
  Multiplexer #(.width(32)) multiplexer_9 (
    .in0(t0_Value), .in1(multiplexer_7_out), .out(t0_write), .sel(RegWrite));  // open: en
  Multiplexer #(.width(32)) multiplexer_10 (
    .in0(t1_Value), .in1(multiplexer_8_out), .out(t1_write), .sel(RegWrite));  // open: en

  // Other names for the same wires on the sheet: CLK = clock; read_reg1[1:0] = Read_register_1;
  //   read_reg2[1:0] = Read_register_2; t0_read[31:0] = t0_Value; t1_read[31:0] = t1_Value; t2_read[31:0] = t2_Value;
  //   t3_read[31:0] = t3_Value

  // Notes on the sheet:
  //   These are INPUTS to the circuit
  //   These are INPUTS to the circuit
  //   DO NOT CHANGE THE LOCATIONS OF THE INPUTS/OUTPUTS! IF YOU DO SO, YOU NEED TO MAKE SURE THE PINS ARE AT THE RIGHT PLACE!
  //   These are OUTPUTS to the circuit
  //   Yet again, the clock is not an actual clock, but an input, one that will be driven from a higher circuit
  //   These are OUTPUTS to the circuit
endmodule
